// Logisim project MiniProjectCopy.circ as structural Verilog: 14 circuits, main circuit main
// 20
module main (
  input  _0,
  input  _1,
  input  _2,
  input  _3,
  input  _4,
  input  _5,
  input  _6,
  input  _7,
  input  _8,
  input  _9,
  input  _0_2,
  input  _1_2,
  input  _2_2,
  input  _3_2,
  input  _4_2,
  input  _5_2,
  input  _6_2,
  input  _7_2,
  input  _8_2,
  input  _9_2,
  input  _0_3,
  input  _1_3,
  input  _2_3,
  input  _3_3,
  input  _4_3,
  input  _5_3,
  input  _6_3,
  input  _7_3,
  input  _8_3,
  input  _9_3,
  input  _0_4,
  input  _1_4,
  input  _2_4,
  input  _3_4,
  input  _4_4,
  input  _5_4,
  input  _6_4,
  input  _7_4,
  input  _8_4,
  input  _9_4
);

  wire arbitrage_validater_1_o0, arbitrage_validater_1_o1, arbitrage_validater_1_o2,
       arbitrage_validater_1_o3, arbitrage_validater_1_o4, arbitrage_validater_1_o5, multiplexer_1_out,
       n2bit_bcd_to_binary_1_o0, n2bit_bcd_to_binary_1_o1, n2bit_bcd_to_binary_1_o2,
       n2bit_bcd_to_binary_1_o3, n2bit_bcd_to_binary_1_o4, n2bit_bcd_to_binary_1_o5,
       n2bit_bcd_to_binary_1_o6, n2bit_bcd_to_binary_2_o0, n2bit_bcd_to_binary_2_o1,
       n2bit_bcd_to_binary_2_o2, n2bit_bcd_to_binary_2_o3, n2bit_bcd_to_binary_2_o4,
       n2bit_bcd_to_binary_2_o5, n2bit_bcd_to_binary_2_o6, n5bit_binfrac_full_adder_1_o0,
       n5bit_binfrac_full_adder_1_o1, n5bit_binfrac_full_adder_1_o2, n5bit_binfrac_full_adder_1_o3,
       n5bit_binfrac_full_adder_1_o4, n5bit_binfrac_full_adder_1_o5, odds_reciprocator_1_q0,
       odds_reciprocator_1_q1, odds_reciprocator_1_q2, odds_reciprocator_1_q3, odds_reciprocator_1_q4,
       odds_reciprocator_1_q5, odds_reciprocator_2_q0, odds_reciprocator_2_q1, odds_reciprocator_2_q2,
       odds_reciprocator_2_q3, odds_reciprocator_2_q4, odds_reciprocator_2_q5, profit_1_1_q1,
       profit_decoder_1_d0_2, profit_decoder_1_d1_2, profit_decoder_1_d2_2, profit_decoder_1_d3_2,
       profit_decoder_1_d4_2, profit_decoder_1_d5, profit_decoder_1_d6, profit_decoder_1_d7,
       profit_decoder_1_d8, profit_decoder_1_d9, profit_decoder_1_d10, profit_decoder_1_d11,
       profit_decoder_1_d12, profit_decoder_1_d13, profit_decoder_1_d14, profit_decoder_1_d15,
       profit_decoder_1_d16, profit_decoder_1_d17, profit_decoder_1_d18, profit_decoder_1_d19,
       profit_decoder_1_d20, profit_divider_1_q0, profit_divider_1_q1, profit_divider_1_q2,
       profit_divider_1_q3, profit_divider_1_q4, profit_divider_1_q5, profit_divider_1_q6;

  _2Bit_BCD_to_Binary u_2bit_bcd_to_binary_1 (
    .D0(_0), .D1(_1), .D2(_2), .D3(_3), .D4(_4), .D5(_5), .D6(_6), .D7(_7), .D8(_8), .D9(_9),
    .D0_prime(_0_2), .D1_prime(_1_2), .D2_prime(_2_2), .D3_prime(_3_2), .D4_prime(_4_2), .D5_prime(_5_2),
    .D6_prime(_6_2), .D7_prime(_7_2), .D8_prime(_8_2), .D9_prime(_9_2), .o0(n2bit_bcd_to_binary_1_o0),
    .o1(n2bit_bcd_to_binary_1_o1), .o2(n2bit_bcd_to_binary_1_o2), .o3(n2bit_bcd_to_binary_1_o3),
    .o4(n2bit_bcd_to_binary_1_o4), .o5(n2bit_bcd_to_binary_1_o5), .o6(n2bit_bcd_to_binary_1_o6));
  _2Bit_BCD_to_Binary u_2bit_bcd_to_binary_2 (
    .D0(_0_3), .D1(_1_3), .D2(_2_3), .D3(_3_3), .D4(_4_3), .D5(_5_3), .D6(_6_3), .D7(_7_3), .D8(_8_3),
    .D9(_9_3), .D0_prime(_0_4), .D1_prime(_1_4), .D2_prime(_2_4), .D3_prime(_3_4), .D4_prime(_4_4),
    .D5_prime(_5_4), .D6_prime(_6_4), .D7_prime(_7_4), .D8_prime(_8_4), .D9_prime(_9_4),
    .o0(n2bit_bcd_to_binary_2_o0), .o1(n2bit_bcd_to_binary_2_o1), .o2(n2bit_bcd_to_binary_2_o2),
    .o3(n2bit_bcd_to_binary_2_o3), .o4(n2bit_bcd_to_binary_2_o4), .o5(n2bit_bcd_to_binary_2_o5),
    .o6(n2bit_bcd_to_binary_2_o6));
  _5Bit_BinFrac_Full_Adder u_5bit_binfrac_full_adder_1 (
    .a0(odds_reciprocator_1_q0), .b0(odds_reciprocator_2_q0), .a1(odds_reciprocator_1_q1),
    .b1(odds_reciprocator_2_q1), .a2(odds_reciprocator_1_q2), .b2(odds_reciprocator_2_q2),
    .a3(odds_reciprocator_1_q3), .b3(odds_reciprocator_2_q3), .a4(odds_reciprocator_1_q4),
    .b4(odds_reciprocator_2_q4), .a5(odds_reciprocator_1_q5), .b5(odds_reciprocator_2_q5),
    .o0(n5bit_binfrac_full_adder_1_o0), .o1(n5bit_binfrac_full_adder_1_o1),
    .o2(n5bit_binfrac_full_adder_1_o2), .o3(n5bit_binfrac_full_adder_1_o3),
    .o4(n5bit_binfrac_full_adder_1_o4), .o5(n5bit_binfrac_full_adder_1_o5));
  Odds_Reciprocator odds_reciprocator_1 (
    .q0(odds_reciprocator_1_q0), .q1(odds_reciprocator_1_q1), .q2(odds_reciprocator_1_q2),
    .q3(odds_reciprocator_1_q3), .q4(odds_reciprocator_1_q4), .q5(odds_reciprocator_1_q5),
    .d0(n2bit_bcd_to_binary_1_o0), .d1(n2bit_bcd_to_binary_1_o1), .d2(n2bit_bcd_to_binary_1_o2),
    .d3(n2bit_bcd_to_binary_1_o3), .d4(n2bit_bcd_to_binary_1_o4), .d5(n2bit_bcd_to_binary_1_o5),
    .d6(n2bit_bcd_to_binary_1_o6));
  Odds_Reciprocator odds_reciprocator_2 (
    .q0(odds_reciprocator_2_q0), .q1(odds_reciprocator_2_q1), .q2(odds_reciprocator_2_q2),
    .q3(odds_reciprocator_2_q3), .q4(odds_reciprocator_2_q4), .q5(odds_reciprocator_2_q5),
    .d0(n2bit_bcd_to_binary_2_o0), .d1(n2bit_bcd_to_binary_2_o1), .d2(n2bit_bcd_to_binary_2_o2),
    .d3(n2bit_bcd_to_binary_2_o3), .d4(n2bit_bcd_to_binary_2_o4), .d5(n2bit_bcd_to_binary_2_o5),
    .d6(n2bit_bcd_to_binary_2_o6));
  Arbitrage_Validater arbitrage_validater_1 (
    .d0(n5bit_binfrac_full_adder_1_o0), .d1(n5bit_binfrac_full_adder_1_o1),
    .d2(n5bit_binfrac_full_adder_1_o2), .d3(n5bit_binfrac_full_adder_1_o3),
    .d4(n5bit_binfrac_full_adder_1_o4), .d5(n5bit_binfrac_full_adder_1_o5), .o0(arbitrage_validater_1_o0),
    .o1(arbitrage_validater_1_o1), .o2(arbitrage_validater_1_o2), .o3(arbitrage_validater_1_o3),
    .o4(arbitrage_validater_1_o4), .o5(arbitrage_validater_1_o5));
  LED led_1 (.in(arbitrage_validater_1_o0));
  Profit_Divider profit_divider_1 (
    .q0(profit_divider_1_q0), .q1(profit_divider_1_q1), .q2(profit_divider_1_q2), .q3(profit_divider_1_q3),
    .q4(profit_divider_1_q4), .q5(profit_divider_1_q5), .q6(profit_divider_1_q6),
    .d0(arbitrage_validater_1_o1), .d1(arbitrage_validater_1_o2), .d2(arbitrage_validater_1_o3),
    .d3(arbitrage_validater_1_o4), .d4(arbitrage_validater_1_o5));
  Profit___1 profit_1_1 (.d1(profit_divider_1_q1), .d0(profit_divider_1_q0), .q1(profit_1_1_q1));  // open: q0
  Multiplexer multiplexer_1 (
    .in0(1'b0), .in1(profit_divider_1_q6), .out(multiplexer_1_out), .sel(arbitrage_validater_1_o0));  // open: en
  Profit__Decoder profit_decoder_1 (
    .D11(profit_decoder_1_d11), .D12(profit_decoder_1_d12), .D13(profit_decoder_1_d13),
    .D14(profit_decoder_1_d14), .D15(profit_decoder_1_d15), .D16(profit_decoder_1_d16),
    .D17(profit_decoder_1_d17), .D18(profit_decoder_1_d18), .D19(profit_decoder_1_d19),
    .D20(profit_decoder_1_d20), .D0_2(profit_decoder_1_d0_2), .D1_2(profit_decoder_1_d1_2),
    .D2_2(profit_decoder_1_d2_2), .D3_2(profit_decoder_1_d3_2), .D4_2(profit_decoder_1_d4_2),
    .D5(profit_decoder_1_d5), .D6(profit_decoder_1_d6), .D7(profit_decoder_1_d7), .D8(profit_decoder_1_d8),
    .D9(profit_decoder_1_d9), .D10(profit_decoder_1_d10), .dMSB(profit_1_1_q1), .d0(profit_divider_1_q2),
    .d1(profit_divider_1_q3), .d2(profit_divider_1_q4), .d3(profit_divider_1_q5), .d4(multiplexer_1_out));
  LED u__0 (.in(profit_decoder_1_d0_2));
  LED u__5 (.in(profit_decoder_1_d1_2));
  LED _10 (.in(profit_decoder_1_d2_2));
  LED _15 (.in(profit_decoder_1_d3_2));
  LED _20 (.in(profit_decoder_1_d4_2));
  LED _25 (.in(profit_decoder_1_d5));
  LED _30 (.in(profit_decoder_1_d6));
  LED _35 (.in(profit_decoder_1_d7));
  LED _40 (.in(profit_decoder_1_d8));
  LED _45 (.in(profit_decoder_1_d9));
  LED _50 (.in(profit_decoder_1_d10));
  LED _55 (.in(profit_decoder_1_d11));
  LED _60 (.in(profit_decoder_1_d12));
  LED _65 (.in(profit_decoder_1_d13));
  LED _70 (.in(profit_decoder_1_d14));
  LED _75 (.in(profit_decoder_1_d15));
  LED _80 (.in(profit_decoder_1_d16));
  LED _85 (.in(profit_decoder_1_d17));
  LED _90 (.in(profit_decoder_1_d18));
  LED _95 (.in(profit_decoder_1_d19));
  LED _100 (.in(profit_decoder_1_d20));

  // Notes on the sheet:
  //   Input1
  //   Team A's
  //   Betting Odds
  //   Input 2
  //   Team B's
  //   Betting Odds
  //   W 
  //   .
  //   X
  //   Y 
  //   .
  //   Z
  //   .
  //   .
  //   BCD To Binary
  //   Converter
  //   BCD To Binary
  //   Converter
  //   Odds -> Probability
  //   DIVIDER
  //   Odds -> Probability
  //   DIVIDER
  //   Full Adder
  //   GUARANTEED PROFITS
  //   WITH ARBITRAGE BETTING!
  //   Find SUM of Probabilities
  //   If Not Arbitrage Bet
  //   Profit is Zero
  //   OUTPUT 1
  //   Binary to Decimal %
  //   CHECK ARBITRAGE BET!
  //   Formula: Profit(%) = (1 / Sum - 1) * 100
  //   OUTPUT 2
  //   MIN GUARANTEED
  //   PROFIT! %
endmodule

module BCD_LSB (
  input  D0,
  input  D1,
  input  D2,
  input  D3,
  input  D4,
  input  D5,
  input  D6,
  input  D7,
  input  D8,
  input  D9,
  output d0_2,
  output d1_2,
  output d2_2,
  output d3_2
);

  or or_1 (d0_2, D8, D9);
  or or_2 (d1_2, D4, D5, D6, D7);
  or or_3 (d2_2, D2, D3, D6, D7);
  or or_4 (d3_2, D1, D3, D5, D7, D9);
endmodule

module BCD_MSB (
  input  D0,
  input  D1,
  input  D2,
  input  D3,
  input  D4,
  input  D5,
  input  D6,
  input  D7,
  input  D8,
  input  D9,
  output d0_2,
  output d1_2,
  output d2_2,
  output d3_2,
  output d4_2,
  output d5_2,
  output d6_2
);

  or or_1 (d0_2, D7, D8, D9);
  or or_2 (d1_2, D4, D5, D6);
  or or_3 (d2_2, D2, D3, D5, D6, D8, D9);
  or or_4 (d3_2, D1, D3, D4, D6, D9);
  or or_5 (d4_2, D2, D3, D6, D7);
  or or_6 (d5_2, D1, D3, D5, D7, D9);

  assign d6_2 = 1'b0;
endmodule

module _7Bit_InitBCD_Full_Adder (
  input  a0,
  input  a1,
  input  a2,
  input  a3,
  input  a4,
  input  a5,
  input  a6,
  input  b0,
  input  b1,
  input  b2,
  input  b3,
  output o0,
  output o1,
  output o2,
  output o3,
  output o4,
  output o5,
  output o6
);

  wire adder_2_cout, adder_3_cout, adder_4_cout, adder_5_cout, adder_6_cout, adder_7_cout;

  Adder #(.width(1)) adder_1 (.a(a0), .b(1'b0), .out(o0), .cin(adder_2_cout));  // open: cout
  Adder #(.width(1)) adder_2 (.a(a1), .b(1'b0), .out(o1), .cin(adder_3_cout), .cout(adder_2_cout));
  Adder #(.width(1)) adder_3 (.a(a2), .b(1'b0), .out(o2), .cin(adder_4_cout), .cout(adder_3_cout));
  Adder #(.width(1)) adder_4 (.a(a3), .b(b0), .out(o3), .cin(adder_5_cout), .cout(adder_4_cout));
  Adder #(.width(1)) adder_5 (.a(a4), .b(b1), .out(o4), .cin(adder_6_cout), .cout(adder_5_cout));
  Adder #(.width(1)) adder_6 (.a(a5), .b(b2), .out(o5), .cin(adder_7_cout), .cout(adder_6_cout));
  Adder #(.width(1)) adder_7 (.a(a6), .b(b3), .out(o6), .cin(1'b0), .cout(adder_7_cout));
endmodule

module _2Bit_BCD_to_Binary (
  input  D0,
  input  D1,
  input  D2,
  input  D3,
  input  D4,
  input  D5,
  input  D6,
  input  D7,
  input  D8,
  input  D9,
  input  D0_prime,
  input  D1_prime,
  input  D2_prime,
  input  D3_prime,
  input  D4_prime,
  input  D5_prime,
  input  D6_prime,
  input  D7_prime,
  input  D8_prime,
  input  D9_prime,
  output o0,
  output o1,
  output o2,
  output o3,
  output o4,
  output o5,
  output o6
);

  wire bcd_lsb_1_d0_2, bcd_lsb_1_d1_2, bcd_lsb_1_d2_2, bcd_lsb_1_d3_2, bcd_msb_1_d0_2, bcd_msb_1_d1_2,
       bcd_msb_1_d2_2, bcd_msb_1_d3_2, bcd_msb_1_d4_2, bcd_msb_1_d5_2, bcd_msb_1_d6_2;

  BCD_MSB bcd_msb_1 (
    .D0(D0), .D1(D1), .D2(D2), .D3(D3), .D4(D4), .D5(D5), .D6(D6), .D7(D7), .D8(D8), .D9(D9),
    .d0_2(bcd_msb_1_d0_2), .d1_2(bcd_msb_1_d1_2), .d2_2(bcd_msb_1_d2_2), .d3_2(bcd_msb_1_d3_2),
    .d4_2(bcd_msb_1_d4_2), .d5_2(bcd_msb_1_d5_2), .d6_2(bcd_msb_1_d6_2));
  BCD_LSB bcd_lsb_1 (
    .D0(D0_prime), .D1(D1_prime), .D2(D2_prime), .D3(D3_prime), .D4(D4_prime), .D5(D5_prime), .D6(D6_prime),
    .D7(D7_prime), .D8(D8_prime), .D9(D9_prime), .d0_2(bcd_lsb_1_d0_2), .d1_2(bcd_lsb_1_d1_2),
    .d2_2(bcd_lsb_1_d2_2), .d3_2(bcd_lsb_1_d3_2));
  _7Bit_InitBCD_Full_Adder u_7bit_initbcd_full_adder_1 (
    .b0(bcd_lsb_1_d0_2), .b1(bcd_lsb_1_d1_2), .b2(bcd_lsb_1_d2_2), .b3(bcd_lsb_1_d3_2), .a0(bcd_msb_1_d0_2),
    .a1(bcd_msb_1_d1_2), .a2(bcd_msb_1_d2_2), .a3(bcd_msb_1_d3_2), .a4(bcd_msb_1_d4_2), .a5(bcd_msb_1_d5_2),
    .a6(bcd_msb_1_d6_2), .o0(o0), .o1(o1), .o2(o2), .o3(o3), .o4(o4), .o5(o5), .o6(o6));
endmodule

module _1Bit___With_Restore (
  input  Cin,
  input  A,
  input  B,
  input  Decider,
  output Decision,
  output Divisior_Prop,
  output Output,
  output Cout
);

  wire adder_1_out, not_1_out;

  Adder #(.width(1)) adder_1 (.a(A), .b(not_1_out), .out(adder_1_out), .cin(Cin), .cout(Cout));
  not not_1 (not_1_out, B);
  Multiplexer multiplexer_1 (.in0(A), .in1(adder_1_out), .out(Output), .sel(Decider), .en(1'b1));

  assign Decision = Decider;
  assign Divisior_Prop = B;

  // Notes on the sheet:
  //   Diff
endmodule

module Odds_Reciprocator (
  input  d0,
  input  d1,
  input  d2,
  input  d3,
  input  d4,
  input  d5,
  input  d6,
  output q0,
  output q1,
  output q2,
  output q3,
  output q4,
  output q5
);

  wire n1bit_with_restore_1_decision, n1bit_with_restore_1_divisior_prop, n1bit_with_restore_1_output,
       n1bit_with_restore_2_decision, n1bit_with_restore_2_divisior_prop, n1bit_with_restore_3_cout,
       n1bit_with_restore_3_decision, n1bit_with_restore_3_divisior_prop, n1bit_with_restore_3_output,
       n1bit_with_restore_4_cout, n1bit_with_restore_4_decision, n1bit_with_restore_4_divisior_prop,
       n1bit_with_restore_4_output, n1bit_with_restore_5_cout, n1bit_with_restore_5_decision,
       n1bit_with_restore_5_divisior_prop, n1bit_with_restore_5_output, n1bit_with_restore_6_cout,
       n1bit_with_restore_6_decision, n1bit_with_restore_6_divisior_prop, n1bit_with_restore_6_output,
       n1bit_with_restore_7_decision, n1bit_with_restore_7_divisior_prop, n1bit_with_restore_8_cout,
       n1bit_with_restore_8_decision, n1bit_with_restore_8_divisior_prop, n1bit_with_restore_8_output,
       n1bit_with_restore_9_decision, n1bit_with_restore_9_divisior_prop, n1bit_with_restore_10_cout,
       n1bit_with_restore_10_decision, n1bit_with_restore_10_divisior_prop, n1bit_with_restore_10_output,
       n1bit_with_restore_11_cout, n1bit_with_restore_11_decision, n1bit_with_restore_11_divisior_prop,
       n1bit_with_restore_11_output, n1bit_with_restore_12_cout, n1bit_with_restore_12_decision,
       n1bit_with_restore_12_divisior_prop, n1bit_with_restore_12_output, n1bit_with_restore_13_cout,
       n1bit_with_restore_13_decision, n1bit_with_restore_13_divisior_prop, n1bit_with_restore_13_output,
       n1bit_with_restore_14_decision, n1bit_with_restore_14_divisior_prop, n1bit_with_restore_15_cout,
       n1bit_with_restore_15_decision, n1bit_with_restore_15_divisior_prop, n1bit_with_restore_15_output,
       n1bit_with_restore_16_cout, n1bit_with_restore_16_decision, n1bit_with_restore_16_divisior_prop,
       n1bit_with_restore_16_output, n1bit_with_restore_17_cout, n1bit_with_restore_17_decision,
       n1bit_with_restore_17_divisior_prop, n1bit_with_restore_17_output, n1bit_with_restore_18_cout,
       n1bit_with_restore_18_decision, n1bit_with_restore_18_divisior_prop, n1bit_with_restore_18_output,
       n1bit_with_restore_19_cout, n1bit_with_restore_19_decision, n1bit_with_restore_19_divisior_prop,
       n1bit_with_restore_19_output, n1bit_with_restore_20_cout, n1bit_with_restore_20_decision,
       n1bit_with_restore_20_divisior_prop, n1bit_with_restore_20_output, n1bit_with_restore_21_cout,
       n1bit_with_restore_21_decision, n1bit_with_restore_21_divisior_prop, n1bit_with_restore_21_output,
       n1bit_with_restore_22_cout, n1bit_with_restore_22_decision, n1bit_with_restore_22_divisior_prop,
       n1bit_with_restore_22_output, n1bit_with_restore_23_cout, n1bit_with_restore_23_decision,
       n1bit_with_restore_23_divisior_prop, n1bit_with_restore_23_output, n1bit_with_restore_24_cout,
       n1bit_with_restore_24_decision, n1bit_with_restore_24_divisior_prop, n1bit_with_restore_24_output,
       n1bit_with_restore_25_decision, n1bit_with_restore_26_cout, n1bit_with_restore_26_decision,
       n1bit_with_restore_27_cout, n1bit_with_restore_27_divisior_prop, n1bit_with_restore_27_output,
       n1bit_with_restore_28_cout, n1bit_with_restore_28_divisior_prop, n1bit_with_restore_28_output,
       n1bit_with_restore_29_cout, n1bit_with_restore_29_decision, n1bit_with_restore_29_divisior_prop,
       n1bit_with_restore_29_output, n1bit_with_restore_30_cout, n1bit_with_restore_30_decision,
       n1bit_with_restore_30_divisior_prop, n1bit_with_restore_30_output, n1bit_with_restore_31_cout,
       n1bit_with_restore_31_decision, n1bit_with_restore_31_divisior_prop, n1bit_with_restore_31_output,
       n1bit_with_restore_32_cout, n1bit_with_restore_32_decision, n1bit_with_restore_32_divisior_prop,
       n1bit_with_restore_32_output, n1bit_with_restore_33_cout, n1bit_with_restore_33_decision,
       n1bit_with_restore_33_divisior_prop, n1bit_with_restore_33_output, n1bit_with_restore_34_cout,
       n1bit_with_restore_34_decision, n1bit_with_restore_34_divisior_prop, n1bit_with_restore_34_output,
       n1bit_with_restore_35_cout, n1bit_with_restore_35_decision, n1bit_with_restore_35_divisior_prop,
       n1bit_with_restore_35_output, n1bit_with_restore_36_cout, n1bit_with_restore_36_decision,
       n1bit_with_restore_37_cout, n1bit_with_restore_37_decision, n1bit_with_restore_38_cout,
       n1bit_with_restore_38_divisior_prop, n1bit_with_restore_38_output, n1bit_with_restore_39_cout,
       n1bit_with_restore_39_decision, n1bit_with_restore_39_divisior_prop, n1bit_with_restore_39_output,
       n1bit_with_restore_40_cout, n1bit_with_restore_40_decision, n1bit_with_restore_40_divisior_prop,
       n1bit_with_restore_40_output, n1bit_with_restore_41_cout, n1bit_with_restore_41_decision,
       n1bit_with_restore_42_cout, n1bit_with_restore_42_divisior_prop, n1bit_with_restore_42_output,
       n1bit_with_restore_43_cout, n1bit_with_restore_43_decision, n1bit_with_restore_43_divisior_prop,
       n1bit_with_restore_43_output, n1bit_with_restore_44_cout, n1bit_with_restore_44_divisior_prop,
       n1bit_with_restore_44_output, n1bit_with_restore_45_cout, n1bit_with_restore_45_decision,
       n1bit_with_restore_46_cout, n1bit_with_restore_46_decision, n1bit_with_restore_47_cout;

  _1Bit___With_Restore u_1bit_with_restore_1 (
    .A(1'b0), .B(d0), .Cin(n1bit_with_restore_3_cout), .Decision(n1bit_with_restore_1_decision), .Cout(q0),
    .Decider(q0), .Divisior_Prop(n1bit_with_restore_1_divisior_prop), .Output(n1bit_with_restore_1_output));
  _1Bit___With_Restore u_1bit_with_restore_2 (
    .A(n1bit_with_restore_1_output), .B(1'b0), .Cin(n1bit_with_restore_5_cout),
    .Decision(n1bit_with_restore_2_decision), .Cout(q1), .Decider(q1),
    .Divisior_Prop(n1bit_with_restore_2_divisior_prop));  // open: Output
  _1Bit___With_Restore u_1bit_with_restore_3 (
    .A(1'b0), .B(d1), .Cin(n1bit_with_restore_4_cout), .Decision(n1bit_with_restore_3_decision),
    .Cout(n1bit_with_restore_3_cout), .Decider(n1bit_with_restore_1_decision),
    .Divisior_Prop(n1bit_with_restore_3_divisior_prop), .Output(n1bit_with_restore_3_output));
  _1Bit___With_Restore u_1bit_with_restore_4 (
    .A(1'b0), .B(d2), .Cin(n1bit_with_restore_10_cout), .Decision(n1bit_with_restore_4_decision),
    .Cout(n1bit_with_restore_4_cout), .Decider(n1bit_with_restore_3_decision),
    .Divisior_Prop(n1bit_with_restore_4_divisior_prop), .Output(n1bit_with_restore_4_output));
  _1Bit___With_Restore u_1bit_with_restore_5 (
    .A(n1bit_with_restore_3_output), .B(n1bit_with_restore_1_divisior_prop), .Cin(n1bit_with_restore_6_cout),
    .Decision(n1bit_with_restore_5_decision), .Cout(n1bit_with_restore_5_cout),
    .Decider(n1bit_with_restore_2_decision), .Divisior_Prop(n1bit_with_restore_5_divisior_prop),
    .Output(n1bit_with_restore_5_output));
  _1Bit___With_Restore u_1bit_with_restore_6 (
    .A(n1bit_with_restore_4_output), .B(n1bit_with_restore_3_divisior_prop),
    .Cin(n1bit_with_restore_11_cout), .Decision(n1bit_with_restore_6_decision),
    .Cout(n1bit_with_restore_6_cout), .Decider(n1bit_with_restore_5_decision),
    .Divisior_Prop(n1bit_with_restore_6_divisior_prop), .Output(n1bit_with_restore_6_output));
  _1Bit___With_Restore u_1bit_with_restore_7 (
    .A(n1bit_with_restore_5_output), .B(n1bit_with_restore_2_divisior_prop), .Cin(n1bit_with_restore_8_cout),
    .Decision(n1bit_with_restore_7_decision), .Cout(q2), .Decider(q2),
    .Divisior_Prop(n1bit_with_restore_7_divisior_prop));  // open: Output
  _1Bit___With_Restore u_1bit_with_restore_8 (
    .A(n1bit_with_restore_6_output), .B(n1bit_with_restore_5_divisior_prop),
    .Cin(n1bit_with_restore_12_cout), .Decision(n1bit_with_restore_8_decision),
    .Cout(n1bit_with_restore_8_cout), .Decider(n1bit_with_restore_7_decision),
    .Divisior_Prop(n1bit_with_restore_8_divisior_prop), .Output(n1bit_with_restore_8_output));
  _1Bit___With_Restore u_1bit_with_restore_9 (
    .A(n1bit_with_restore_8_output), .B(n1bit_with_restore_7_divisior_prop),
    .Cin(n1bit_with_restore_13_cout), .Decision(n1bit_with_restore_9_decision), .Cout(q3), .Decider(q3),
    .Divisior_Prop(n1bit_with_restore_9_divisior_prop));  // open: Output
  _1Bit___With_Restore u_1bit_with_restore_10 (
    .A(1'b1), .B(d3), .Cin(n1bit_with_restore_15_cout), .Decision(n1bit_with_restore_10_decision),
    .Cout(n1bit_with_restore_10_cout), .Decider(n1bit_with_restore_4_decision),
    .Divisior_Prop(n1bit_with_restore_10_divisior_prop), .Output(n1bit_with_restore_10_output));
  _1Bit___With_Restore u_1bit_with_restore_11 (
    .A(n1bit_with_restore_10_output), .B(n1bit_with_restore_4_divisior_prop),
    .Cin(n1bit_with_restore_18_cout), .Decision(n1bit_with_restore_11_decision),
    .Cout(n1bit_with_restore_11_cout), .Decider(n1bit_with_restore_6_decision),
    .Divisior_Prop(n1bit_with_restore_11_divisior_prop), .Output(n1bit_with_restore_11_output));
  _1Bit___With_Restore u_1bit_with_restore_12 (
    .A(n1bit_with_restore_11_output), .B(n1bit_with_restore_6_divisior_prop),
    .Cin(n1bit_with_restore_20_cout), .Decision(n1bit_with_restore_12_decision),
    .Cout(n1bit_with_restore_12_cout), .Decider(n1bit_with_restore_8_decision),
    .Divisior_Prop(n1bit_with_restore_12_divisior_prop), .Output(n1bit_with_restore_12_output));
  _1Bit___With_Restore u_1bit_with_restore_13 (
    .A(n1bit_with_restore_12_output), .B(n1bit_with_restore_8_divisior_prop),
    .Cin(n1bit_with_restore_21_cout), .Decision(n1bit_with_restore_13_decision),
    .Cout(n1bit_with_restore_13_cout), .Decider(n1bit_with_restore_9_decision),
    .Divisior_Prop(n1bit_with_restore_13_divisior_prop), .Output(n1bit_with_restore_13_output));
  _1Bit___With_Restore u_1bit_with_restore_14 (
    .A(n1bit_with_restore_13_output), .B(n1bit_with_restore_9_divisior_prop),
    .Cin(n1bit_with_restore_24_cout), .Decision(n1bit_with_restore_14_decision), .Cout(q4), .Decider(q4),
    .Divisior_Prop(n1bit_with_restore_14_divisior_prop));  // open: Output
  _1Bit___With_Restore u_1bit_with_restore_15 (
    .A(1'b0), .B(d4), .Cin(n1bit_with_restore_16_cout), .Decision(n1bit_with_restore_15_decision),
    .Cout(n1bit_with_restore_15_cout), .Decider(n1bit_with_restore_10_decision),
    .Divisior_Prop(n1bit_with_restore_15_divisior_prop), .Output(n1bit_with_restore_15_output));
  _1Bit___With_Restore u_1bit_with_restore_16 (
    .A(1'b1), .B(d5), .Cin(n1bit_with_restore_27_cout), .Decision(n1bit_with_restore_16_decision),
    .Cout(n1bit_with_restore_16_cout), .Decider(n1bit_with_restore_15_decision),
    .Divisior_Prop(n1bit_with_restore_16_divisior_prop), .Output(n1bit_with_restore_16_output));
  _1Bit___With_Restore u_1bit_with_restore_17 (
    .A(n1bit_with_restore_16_output), .B(n1bit_with_restore_15_divisior_prop),
    .Cin(n1bit_with_restore_29_cout), .Decision(n1bit_with_restore_17_decision),
    .Cout(n1bit_with_restore_17_cout), .Decider(n1bit_with_restore_18_decision),
    .Divisior_Prop(n1bit_with_restore_17_divisior_prop), .Output(n1bit_with_restore_17_output));
  _1Bit___With_Restore u_1bit_with_restore_18 (
    .A(n1bit_with_restore_15_output), .B(n1bit_with_restore_10_divisior_prop),
    .Cin(n1bit_with_restore_17_cout), .Decision(n1bit_with_restore_18_decision),
    .Cout(n1bit_with_restore_18_cout), .Decider(n1bit_with_restore_11_decision),
    .Divisior_Prop(n1bit_with_restore_18_divisior_prop), .Output(n1bit_with_restore_18_output));
  _1Bit___With_Restore u_1bit_with_restore_19 (
    .A(n1bit_with_restore_17_output), .B(n1bit_with_restore_18_divisior_prop),
    .Cin(n1bit_with_restore_30_cout), .Decision(n1bit_with_restore_19_decision),
    .Cout(n1bit_with_restore_19_cout), .Decider(n1bit_with_restore_20_decision),
    .Divisior_Prop(n1bit_with_restore_19_divisior_prop), .Output(n1bit_with_restore_19_output));
  _1Bit___With_Restore u_1bit_with_restore_20 (
    .A(n1bit_with_restore_18_output), .B(n1bit_with_restore_11_divisior_prop),
    .Cin(n1bit_with_restore_19_cout), .Decision(n1bit_with_restore_20_decision),
    .Cout(n1bit_with_restore_20_cout), .Decider(n1bit_with_restore_12_decision),
    .Divisior_Prop(n1bit_with_restore_20_divisior_prop), .Output(n1bit_with_restore_20_output));
  _1Bit___With_Restore u_1bit_with_restore_21 (
    .A(n1bit_with_restore_20_output), .B(n1bit_with_restore_12_divisior_prop),
    .Cin(n1bit_with_restore_22_cout), .Decision(n1bit_with_restore_21_decision),
    .Cout(n1bit_with_restore_21_cout), .Decider(n1bit_with_restore_13_decision),
    .Divisior_Prop(n1bit_with_restore_21_divisior_prop), .Output(n1bit_with_restore_21_output));
  _1Bit___With_Restore u_1bit_with_restore_22 (
    .A(n1bit_with_restore_19_output), .B(n1bit_with_restore_20_divisior_prop),
    .Cin(n1bit_with_restore_32_cout), .Decision(n1bit_with_restore_22_decision),
    .Cout(n1bit_with_restore_22_cout), .Decider(n1bit_with_restore_21_decision),
    .Divisior_Prop(n1bit_with_restore_22_divisior_prop), .Output(n1bit_with_restore_22_output));
  _1Bit___With_Restore u_1bit_with_restore_23 (
    .A(n1bit_with_restore_22_output), .B(n1bit_with_restore_21_divisior_prop),
    .Cin(n1bit_with_restore_35_cout), .Decision(n1bit_with_restore_23_decision),
    .Cout(n1bit_with_restore_23_cout), .Decider(n1bit_with_restore_24_decision),
    .Divisior_Prop(n1bit_with_restore_23_divisior_prop), .Output(n1bit_with_restore_23_output));
  _1Bit___With_Restore u_1bit_with_restore_24 (
    .A(n1bit_with_restore_21_output), .B(n1bit_with_restore_13_divisior_prop),
    .Cin(n1bit_with_restore_23_cout), .Decision(n1bit_with_restore_24_decision),
    .Cout(n1bit_with_restore_24_cout), .Decider(n1bit_with_restore_14_decision),
    .Divisior_Prop(n1bit_with_restore_24_divisior_prop), .Output(n1bit_with_restore_24_output));
  _1Bit___With_Restore u_1bit_with_restore_25 (
    .A(n1bit_with_restore_24_output), .B(n1bit_with_restore_14_divisior_prop),
    .Cin(n1bit_with_restore_26_cout), .Decision(n1bit_with_restore_25_decision), .Cout(q5), .Decider(q5));  // open: Divisior_Prop, Output
  _1Bit___With_Restore u_1bit_with_restore_26 (
    .A(n1bit_with_restore_23_output), .B(n1bit_with_restore_24_divisior_prop),
    .Cin(n1bit_with_restore_37_cout), .Decision(n1bit_with_restore_26_decision),
    .Cout(n1bit_with_restore_26_cout), .Decider(n1bit_with_restore_25_decision));  // open: Divisior_Prop, Output
  _1Bit___With_Restore u_1bit_with_restore_27 (
    .A(1'b0), .B(d6), .Cin(1'b1), .Cout(n1bit_with_restore_27_cout),
    .Decider(n1bit_with_restore_16_decision), .Divisior_Prop(n1bit_with_restore_27_divisior_prop),
    .Output(n1bit_with_restore_27_output));  // open: Decision
  _1Bit___With_Restore u_1bit_with_restore_28 (
    .A(1'b0), .B(n1bit_with_restore_27_divisior_prop), .Cin(1'b1), .Cout(n1bit_with_restore_28_cout),
    .Decider(n1bit_with_restore_29_decision), .Divisior_Prop(n1bit_with_restore_28_divisior_prop),
    .Output(n1bit_with_restore_28_output));  // open: Decision
  _1Bit___With_Restore u_1bit_with_restore_29 (
    .A(n1bit_with_restore_27_output), .B(n1bit_with_restore_16_divisior_prop),
    .Cin(n1bit_with_restore_28_cout), .Decision(n1bit_with_restore_29_decision),
    .Cout(n1bit_with_restore_29_cout), .Decider(n1bit_with_restore_17_decision),
    .Divisior_Prop(n1bit_with_restore_29_divisior_prop), .Output(n1bit_with_restore_29_output));
  _1Bit___With_Restore u_1bit_with_restore_30 (
    .A(n1bit_with_restore_29_output), .B(n1bit_with_restore_17_divisior_prop),
    .Cin(n1bit_with_restore_31_cout), .Decision(n1bit_with_restore_30_decision),
    .Cout(n1bit_with_restore_30_cout), .Decider(n1bit_with_restore_19_decision),
    .Divisior_Prop(n1bit_with_restore_30_divisior_prop), .Output(n1bit_with_restore_30_output));
  _1Bit___With_Restore u_1bit_with_restore_31 (
    .A(n1bit_with_restore_28_output), .B(n1bit_with_restore_29_divisior_prop),
    .Cin(n1bit_with_restore_38_cout), .Decision(n1bit_with_restore_31_decision),
    .Cout(n1bit_with_restore_31_cout), .Decider(n1bit_with_restore_30_decision),
    .Divisior_Prop(n1bit_with_restore_31_divisior_prop), .Output(n1bit_with_restore_31_output));
  _1Bit___With_Restore u_1bit_with_restore_32 (
    .A(n1bit_with_restore_30_output), .B(n1bit_with_restore_19_divisior_prop),
    .Cin(n1bit_with_restore_33_cout), .Decision(n1bit_with_restore_32_decision),
    .Cout(n1bit_with_restore_32_cout), .Decider(n1bit_with_restore_22_decision),
    .Divisior_Prop(n1bit_with_restore_32_divisior_prop), .Output(n1bit_with_restore_32_output));
  _1Bit___With_Restore u_1bit_with_restore_33 (
    .A(n1bit_with_restore_31_output), .B(n1bit_with_restore_30_divisior_prop),
    .Cin(n1bit_with_restore_39_cout), .Decision(n1bit_with_restore_33_decision),
    .Cout(n1bit_with_restore_33_cout), .Decider(n1bit_with_restore_32_decision),
    .Divisior_Prop(n1bit_with_restore_33_divisior_prop), .Output(n1bit_with_restore_33_output));
  _1Bit___With_Restore u_1bit_with_restore_34 (
    .A(n1bit_with_restore_33_output), .B(n1bit_with_restore_32_divisior_prop),
    .Cin(n1bit_with_restore_40_cout), .Decision(n1bit_with_restore_34_decision),
    .Cout(n1bit_with_restore_34_cout), .Decider(n1bit_with_restore_35_decision),
    .Divisior_Prop(n1bit_with_restore_34_divisior_prop), .Output(n1bit_with_restore_34_output));
  _1Bit___With_Restore u_1bit_with_restore_35 (
    .A(n1bit_with_restore_32_output), .B(n1bit_with_restore_22_divisior_prop),
    .Cin(n1bit_with_restore_34_cout), .Decision(n1bit_with_restore_35_decision),
    .Cout(n1bit_with_restore_35_cout), .Decider(n1bit_with_restore_23_decision),
    .Divisior_Prop(n1bit_with_restore_35_divisior_prop), .Output(n1bit_with_restore_35_output));
  _1Bit___With_Restore u_1bit_with_restore_36 (
    .A(n1bit_with_restore_34_output), .B(n1bit_with_restore_35_divisior_prop),
    .Cin(n1bit_with_restore_41_cout), .Decision(n1bit_with_restore_36_decision),
    .Cout(n1bit_with_restore_36_cout), .Decider(n1bit_with_restore_37_decision));  // open: Divisior_Prop, Output
  _1Bit___With_Restore u_1bit_with_restore_37 (
    .A(n1bit_with_restore_35_output), .B(n1bit_with_restore_23_divisior_prop),
    .Cin(n1bit_with_restore_36_cout), .Decision(n1bit_with_restore_37_decision),
    .Cout(n1bit_with_restore_37_cout), .Decider(n1bit_with_restore_26_decision));  // open: Divisior_Prop, Output
  _1Bit___With_Restore u_1bit_with_restore_38 (
    .A(1'b0), .B(n1bit_with_restore_28_divisior_prop), .Cin(1'b1), .Cout(n1bit_with_restore_38_cout),
    .Decider(n1bit_with_restore_31_decision), .Divisior_Prop(n1bit_with_restore_38_divisior_prop),
    .Output(n1bit_with_restore_38_output));  // open: Decision
  _1Bit___With_Restore u_1bit_with_restore_39 (
    .A(n1bit_with_restore_38_output), .B(n1bit_with_restore_31_divisior_prop),
    .Cin(n1bit_with_restore_42_cout), .Decision(n1bit_with_restore_39_decision),
    .Cout(n1bit_with_restore_39_cout), .Decider(n1bit_with_restore_33_decision),
    .Divisior_Prop(n1bit_with_restore_39_divisior_prop), .Output(n1bit_with_restore_39_output));
  _1Bit___With_Restore u_1bit_with_restore_40 (
    .A(n1bit_with_restore_39_output), .B(n1bit_with_restore_33_divisior_prop),
    .Cin(n1bit_with_restore_43_cout), .Decision(n1bit_with_restore_40_decision),
    .Cout(n1bit_with_restore_40_cout), .Decider(n1bit_with_restore_34_decision),
    .Divisior_Prop(n1bit_with_restore_40_divisior_prop), .Output(n1bit_with_restore_40_output));
  _1Bit___With_Restore u_1bit_with_restore_41 (
    .A(n1bit_with_restore_40_output), .B(n1bit_with_restore_34_divisior_prop),
    .Cin(n1bit_with_restore_46_cout), .Decision(n1bit_with_restore_41_decision),
    .Cout(n1bit_with_restore_41_cout), .Decider(n1bit_with_restore_36_decision));  // open: Divisior_Prop, Output
  _1Bit___With_Restore u_1bit_with_restore_42 (
    .A(1'b0), .B(n1bit_with_restore_38_divisior_prop), .Cin(1'b1), .Cout(n1bit_with_restore_42_cout),
    .Decider(n1bit_with_restore_39_decision), .Divisior_Prop(n1bit_with_restore_42_divisior_prop),
    .Output(n1bit_with_restore_42_output));  // open: Decision
  _1Bit___With_Restore u_1bit_with_restore_43 (
    .A(n1bit_with_restore_42_output), .B(n1bit_with_restore_39_divisior_prop),
    .Cin(n1bit_with_restore_44_cout), .Decision(n1bit_with_restore_43_decision),
    .Cout(n1bit_with_restore_43_cout), .Decider(n1bit_with_restore_40_decision),
    .Divisior_Prop(n1bit_with_restore_43_divisior_prop), .Output(n1bit_with_restore_43_output));
  _1Bit___With_Restore u_1bit_with_restore_44 (
    .A(1'b0), .B(n1bit_with_restore_42_divisior_prop), .Cin(1'b1), .Cout(n1bit_with_restore_44_cout),
    .Decider(n1bit_with_restore_43_decision), .Divisior_Prop(n1bit_with_restore_44_divisior_prop),
    .Output(n1bit_with_restore_44_output));  // open: Decision
  _1Bit___With_Restore u_1bit_with_restore_45 (
    .A(n1bit_with_restore_44_output), .B(n1bit_with_restore_43_divisior_prop),
    .Cin(n1bit_with_restore_47_cout), .Decision(n1bit_with_restore_45_decision),
    .Cout(n1bit_with_restore_45_cout), .Decider(n1bit_with_restore_46_decision));  // open: Divisior_Prop, Output
  _1Bit___With_Restore u_1bit_with_restore_46 (
    .A(n1bit_with_restore_43_output), .B(n1bit_with_restore_40_divisior_prop),
    .Cin(n1bit_with_restore_45_cout), .Decision(n1bit_with_restore_46_decision),
    .Cout(n1bit_with_restore_46_cout), .Decider(n1bit_with_restore_41_decision));  // open: Divisior_Prop, Output
  _1Bit___With_Restore u_1bit_with_restore_47 (
    .A(1'b0), .B(n1bit_with_restore_44_divisior_prop), .Cin(1'b1), .Cout(n1bit_with_restore_47_cout),
    .Decider(n1bit_with_restore_45_decision));  // open: Decision, Divisior_Prop, Output

  // Notes on the sheet:
  //   .
  //   .
  //   Credit: ALL ABOUT ELECTRONICS
endmodule

module _5Bit_BinFrac_Full_Adder (
  input  a0,
  input  a1,
  input  a2,
  input  a3,
  input  a4,
  input  a5,
  input  b0,
  input  b1,
  input  b2,
  input  b3,
  input  b4,
  input  b5,
  output o0,
  output o1,
  output o2,
  output o3,
  output o4,
  output o5
);

  wire adder_2_cout, adder_3_cout, adder_4_cout, adder_5_cout, adder_6_cout;

  Adder #(.width(1)) adder_1 (.a(a0), .b(b0), .out(o0), .cin(adder_2_cout));  // open: cout
  Adder #(.width(1)) adder_2 (.a(a1), .b(b1), .out(o1), .cin(adder_3_cout), .cout(adder_2_cout));
  Adder #(.width(1)) adder_3 (.a(a2), .b(b2), .out(o2), .cin(adder_4_cout), .cout(adder_3_cout));
  Adder #(.width(1)) adder_4 (.a(a3), .b(b3), .out(o3), .cin(adder_5_cout), .cout(adder_4_cout));
  Adder #(.width(1)) adder_5 (.a(a4), .b(b4), .out(o4), .cin(adder_6_cout), .cout(adder_5_cout));
  Adder #(.width(1)) adder_6 (.a(a5), .b(b5), .out(o5), .cin(1'b0), .cout(adder_6_cout));

  // Notes on the sheet:
  //   .
  //   .
  //   .
endmodule

module _1_Comparator (
  input  Checking,
  output Arbitrage
);

  not not_1 (Arbitrage, Checking);
endmodule

module Arbitrage_Validater (
  input  d0,
  input  d1,
  input  d2,
  input  d3,
  input  d4,
  input  d5,
  output o0,
  output o1,
  output o2,
  output o3,
  output o4,
  output o5
);

  _1_Comparator u_1_comparator_1 (.Checking(d0), .Arbitrage(o0));
  Multiplexer multiplexer_1 (.in0(1'b1), .in1(d1), .out(o1), .sel(o0));  // open: en
  Multiplexer multiplexer_2 (.in0(1'b1), .in1(d2), .out(o2), .sel(o0));  // open: en
  Multiplexer multiplexer_3 (.in0(1'b1), .in1(d3), .out(o3), .sel(o0));  // open: en
  Multiplexer multiplexer_4 (.in0(1'b1), .in1(d4), .out(o4), .sel(o0));  // open: en
  Multiplexer multiplexer_5 (.in0(1'b1), .in1(d5), .out(o5), .sel(o0));  // open: en
endmodule

module Profit_Divider (
  input  d0,
  input  d1,
  input  d2,
  input  d3,
  input  d4,
  output q0,
  output q1,
  output q2,
  output q3,
  output q4,
  output q5,
  output q6
);

  wire n1bit_with_restore_1_decision, n1bit_with_restore_1_divisior_prop, n1bit_with_restore_1_output,
       n1bit_with_restore_2_decision, n1bit_with_restore_2_divisior_prop, n1bit_with_restore_3_cout,
       n1bit_with_restore_3_decision, n1bit_with_restore_3_divisior_prop, n1bit_with_restore_3_output,
       n1bit_with_restore_4_cout, n1bit_with_restore_4_decision, n1bit_with_restore_4_divisior_prop,
       n1bit_with_restore_4_output, n1bit_with_restore_5_cout, n1bit_with_restore_5_decision,
       n1bit_with_restore_5_divisior_prop, n1bit_with_restore_5_output, n1bit_with_restore_6_cout,
       n1bit_with_restore_6_decision, n1bit_with_restore_6_divisior_prop, n1bit_with_restore_6_output,
       n1bit_with_restore_7_decision, n1bit_with_restore_7_divisior_prop, n1bit_with_restore_8_cout,
       n1bit_with_restore_8_decision, n1bit_with_restore_8_divisior_prop, n1bit_with_restore_8_output,
       n1bit_with_restore_9_decision, n1bit_with_restore_9_divisior_prop, n1bit_with_restore_10_cout,
       n1bit_with_restore_10_decision, n1bit_with_restore_10_divisior_prop, n1bit_with_restore_10_output,
       n1bit_with_restore_11_cout, n1bit_with_restore_11_decision, n1bit_with_restore_11_divisior_prop,
       n1bit_with_restore_11_output, n1bit_with_restore_12_cout, n1bit_with_restore_12_decision,
       n1bit_with_restore_12_divisior_prop, n1bit_with_restore_12_output, n1bit_with_restore_13_cout,
       n1bit_with_restore_13_decision, n1bit_with_restore_13_divisior_prop, n1bit_with_restore_13_output,
       n1bit_with_restore_14_decision, n1bit_with_restore_14_divisior_prop, n1bit_with_restore_15_cout,
       n1bit_with_restore_15_divisior_prop, n1bit_with_restore_15_output, n1bit_with_restore_16_cout,
       n1bit_with_restore_16_decision, n1bit_with_restore_16_divisior_prop, n1bit_with_restore_16_output,
       n1bit_with_restore_17_cout, n1bit_with_restore_17_decision, n1bit_with_restore_17_divisior_prop,
       n1bit_with_restore_17_output, n1bit_with_restore_18_cout, n1bit_with_restore_18_decision,
       n1bit_with_restore_18_divisior_prop, n1bit_with_restore_18_output, n1bit_with_restore_19_cout,
       n1bit_with_restore_19_decision, n1bit_with_restore_19_divisior_prop, n1bit_with_restore_19_output,
       n1bit_with_restore_20_decision, n1bit_with_restore_20_divisior_prop, n1bit_with_restore_21_cout,
       n1bit_with_restore_21_divisior_prop, n1bit_with_restore_21_output, n1bit_with_restore_22_cout,
       n1bit_with_restore_22_divisior_prop, n1bit_with_restore_22_output, n1bit_with_restore_23_cout,
       n1bit_with_restore_23_decision, n1bit_with_restore_23_divisior_prop, n1bit_with_restore_23_output,
       n1bit_with_restore_24_cout, n1bit_with_restore_24_decision, n1bit_with_restore_24_divisior_prop,
       n1bit_with_restore_24_output, n1bit_with_restore_25_cout, n1bit_with_restore_25_decision,
       n1bit_with_restore_25_divisior_prop, n1bit_with_restore_25_output, n1bit_with_restore_26_cout,
       n1bit_with_restore_26_decision, n1bit_with_restore_26_divisior_prop, n1bit_with_restore_26_output,
       n1bit_with_restore_27_cout, n1bit_with_restore_27_decision, n1bit_with_restore_27_divisior_prop,
       n1bit_with_restore_27_output, n1bit_with_restore_28_cout, n1bit_with_restore_28_decision,
       n1bit_with_restore_28_divisior_prop, n1bit_with_restore_28_output, n1bit_with_restore_29_cout,
       n1bit_with_restore_29_decision, n1bit_with_restore_29_divisior_prop, n1bit_with_restore_29_output,
       n1bit_with_restore_30_cout, n1bit_with_restore_30_decision, n1bit_with_restore_31_decision,
       n1bit_with_restore_32_cout, n1bit_with_restore_32_divisior_prop, n1bit_with_restore_32_output,
       n1bit_with_restore_33_cout, n1bit_with_restore_33_decision, n1bit_with_restore_33_divisior_prop,
       n1bit_with_restore_33_output, n1bit_with_restore_34_cout, n1bit_with_restore_34_decision,
       n1bit_with_restore_34_divisior_prop, n1bit_with_restore_34_output, n1bit_with_restore_35_cout,
       n1bit_with_restore_35_decision, n1bit_with_restore_36_cout, n1bit_with_restore_36_divisior_prop,
       n1bit_with_restore_36_output, n1bit_with_restore_37_cout, n1bit_with_restore_37_decision,
       n1bit_with_restore_37_divisior_prop, n1bit_with_restore_37_output, n1bit_with_restore_38_cout,
       n1bit_with_restore_38_decision, n1bit_with_restore_39_cout, n1bit_with_restore_39_divisior_prop,
       n1bit_with_restore_39_output, n1bit_with_restore_40_cout, n1bit_with_restore_41_cout,
       n1bit_with_restore_41_decision;

  _1Bit___With_Restore u_1bit_with_restore_1 (
    .A(1'b1), .B(d0), .Cin(n1bit_with_restore_4_cout), .Decision(n1bit_with_restore_1_decision), .Cout(q0),
    .Decider(q0), .Divisior_Prop(n1bit_with_restore_1_divisior_prop), .Output(n1bit_with_restore_1_output));
  _1Bit___With_Restore u_1bit_with_restore_2 (
    .A(n1bit_with_restore_1_output), .B(1'b0), .Cin(n1bit_with_restore_5_cout),
    .Decision(n1bit_with_restore_2_decision), .Cout(q1), .Decider(q1),
    .Divisior_Prop(n1bit_with_restore_2_divisior_prop));  // open: Output
  _1Bit___With_Restore u_1bit_with_restore_3 (
    .A(1'b0), .B(d2), .Cin(n1bit_with_restore_10_cout), .Decision(n1bit_with_restore_3_decision),
    .Cout(n1bit_with_restore_3_cout), .Decider(n1bit_with_restore_4_decision),
    .Divisior_Prop(n1bit_with_restore_3_divisior_prop), .Output(n1bit_with_restore_3_output));
  _1Bit___With_Restore u_1bit_with_restore_4 (
    .A(1'b0), .B(d1), .Cin(n1bit_with_restore_3_cout), .Decision(n1bit_with_restore_4_decision),
    .Cout(n1bit_with_restore_4_cout), .Decider(n1bit_with_restore_1_decision),
    .Divisior_Prop(n1bit_with_restore_4_divisior_prop), .Output(n1bit_with_restore_4_output));
  _1Bit___With_Restore u_1bit_with_restore_5 (
    .A(n1bit_with_restore_4_output), .B(n1bit_with_restore_1_divisior_prop), .Cin(n1bit_with_restore_6_cout),
    .Decision(n1bit_with_restore_5_decision), .Cout(n1bit_with_restore_5_cout),
    .Decider(n1bit_with_restore_2_decision), .Divisior_Prop(n1bit_with_restore_5_divisior_prop),
    .Output(n1bit_with_restore_5_output));
  _1Bit___With_Restore u_1bit_with_restore_6 (
    .A(n1bit_with_restore_3_output), .B(n1bit_with_restore_4_divisior_prop),
    .Cin(n1bit_with_restore_11_cout), .Decision(n1bit_with_restore_6_decision),
    .Cout(n1bit_with_restore_6_cout), .Decider(n1bit_with_restore_5_decision),
    .Divisior_Prop(n1bit_with_restore_6_divisior_prop), .Output(n1bit_with_restore_6_output));
  _1Bit___With_Restore u_1bit_with_restore_7 (
    .A(n1bit_with_restore_5_output), .B(n1bit_with_restore_2_divisior_prop), .Cin(n1bit_with_restore_8_cout),
    .Decision(n1bit_with_restore_7_decision), .Cout(q2), .Decider(q2),
    .Divisior_Prop(n1bit_with_restore_7_divisior_prop));  // open: Output
  _1Bit___With_Restore u_1bit_with_restore_8 (
    .A(n1bit_with_restore_6_output), .B(n1bit_with_restore_5_divisior_prop),
    .Cin(n1bit_with_restore_12_cout), .Decision(n1bit_with_restore_8_decision),
    .Cout(n1bit_with_restore_8_cout), .Decider(n1bit_with_restore_7_decision),
    .Divisior_Prop(n1bit_with_restore_8_divisior_prop), .Output(n1bit_with_restore_8_output));
  _1Bit___With_Restore u_1bit_with_restore_9 (
    .A(n1bit_with_restore_8_output), .B(n1bit_with_restore_7_divisior_prop),
    .Cin(n1bit_with_restore_13_cout), .Decision(n1bit_with_restore_9_decision), .Cout(q3), .Decider(q3),
    .Divisior_Prop(n1bit_with_restore_9_divisior_prop));  // open: Output
  _1Bit___With_Restore u_1bit_with_restore_10 (
    .A(1'b0), .B(d3), .Cin(n1bit_with_restore_15_cout), .Decision(n1bit_with_restore_10_decision),
    .Cout(n1bit_with_restore_10_cout), .Decider(n1bit_with_restore_3_decision),
    .Divisior_Prop(n1bit_with_restore_10_divisior_prop), .Output(n1bit_with_restore_10_output));
  _1Bit___With_Restore u_1bit_with_restore_11 (
    .A(n1bit_with_restore_10_output), .B(n1bit_with_restore_3_divisior_prop),
    .Cin(n1bit_with_restore_16_cout), .Decision(n1bit_with_restore_11_decision),
    .Cout(n1bit_with_restore_11_cout), .Decider(n1bit_with_restore_6_decision),
    .Divisior_Prop(n1bit_with_restore_11_divisior_prop), .Output(n1bit_with_restore_11_output));
  _1Bit___With_Restore u_1bit_with_restore_12 (
    .A(n1bit_with_restore_11_output), .B(n1bit_with_restore_6_divisior_prop),
    .Cin(n1bit_with_restore_17_cout), .Decision(n1bit_with_restore_12_decision),
    .Cout(n1bit_with_restore_12_cout), .Decider(n1bit_with_restore_8_decision),
    .Divisior_Prop(n1bit_with_restore_12_divisior_prop), .Output(n1bit_with_restore_12_output));
  _1Bit___With_Restore u_1bit_with_restore_13 (
    .A(n1bit_with_restore_12_output), .B(n1bit_with_restore_8_divisior_prop),
    .Cin(n1bit_with_restore_18_cout), .Decision(n1bit_with_restore_13_decision),
    .Cout(n1bit_with_restore_13_cout), .Decider(n1bit_with_restore_9_decision),
    .Divisior_Prop(n1bit_with_restore_13_divisior_prop), .Output(n1bit_with_restore_13_output));
  _1Bit___With_Restore u_1bit_with_restore_14 (
    .A(n1bit_with_restore_13_output), .B(n1bit_with_restore_9_divisior_prop),
    .Cin(n1bit_with_restore_19_cout), .Decision(n1bit_with_restore_14_decision), .Cout(q4), .Decider(q4),
    .Divisior_Prop(n1bit_with_restore_14_divisior_prop));  // open: Output
  _1Bit___With_Restore u_1bit_with_restore_15 (
    .A(1'b0), .B(d4), .Cin(1'b1), .Cout(n1bit_with_restore_15_cout),
    .Decider(n1bit_with_restore_10_decision), .Divisior_Prop(n1bit_with_restore_15_divisior_prop),
    .Output(n1bit_with_restore_15_output));  // open: Decision
  _1Bit___With_Restore u_1bit_with_restore_16 (
    .A(n1bit_with_restore_15_output), .B(n1bit_with_restore_10_divisior_prop),
    .Cin(n1bit_with_restore_21_cout), .Decision(n1bit_with_restore_16_decision),
    .Cout(n1bit_with_restore_16_cout), .Decider(n1bit_with_restore_11_decision),
    .Divisior_Prop(n1bit_with_restore_16_divisior_prop), .Output(n1bit_with_restore_16_output));
  _1Bit___With_Restore u_1bit_with_restore_17 (
    .A(n1bit_with_restore_16_output), .B(n1bit_with_restore_11_divisior_prop),
    .Cin(n1bit_with_restore_23_cout), .Decision(n1bit_with_restore_17_decision),
    .Cout(n1bit_with_restore_17_cout), .Decider(n1bit_with_restore_12_decision),
    .Divisior_Prop(n1bit_with_restore_17_divisior_prop), .Output(n1bit_with_restore_17_output));
  _1Bit___With_Restore u_1bit_with_restore_18 (
    .A(n1bit_with_restore_17_output), .B(n1bit_with_restore_12_divisior_prop),
    .Cin(n1bit_with_restore_24_cout), .Decision(n1bit_with_restore_18_decision),
    .Cout(n1bit_with_restore_18_cout), .Decider(n1bit_with_restore_13_decision),
    .Divisior_Prop(n1bit_with_restore_18_divisior_prop), .Output(n1bit_with_restore_18_output));
  _1Bit___With_Restore u_1bit_with_restore_19 (
    .A(n1bit_with_restore_18_output), .B(n1bit_with_restore_13_divisior_prop),
    .Cin(n1bit_with_restore_27_cout), .Decision(n1bit_with_restore_19_decision),
    .Cout(n1bit_with_restore_19_cout), .Decider(n1bit_with_restore_14_decision),
    .Divisior_Prop(n1bit_with_restore_19_divisior_prop), .Output(n1bit_with_restore_19_output));
  _1Bit___With_Restore u_1bit_with_restore_20 (
    .A(n1bit_with_restore_19_output), .B(n1bit_with_restore_14_divisior_prop),
    .Cin(n1bit_with_restore_29_cout), .Decision(n1bit_with_restore_20_decision), .Cout(q5), .Decider(q5),
    .Divisior_Prop(n1bit_with_restore_20_divisior_prop));  // open: Output
  _1Bit___With_Restore u_1bit_with_restore_21 (
    .A(1'b0), .B(n1bit_with_restore_15_divisior_prop), .Cin(1'b1), .Cout(n1bit_with_restore_21_cout),
    .Decider(n1bit_with_restore_16_decision), .Divisior_Prop(n1bit_with_restore_21_divisior_prop),
    .Output(n1bit_with_restore_21_output));  // open: Decision
  _1Bit___With_Restore u_1bit_with_restore_22 (
    .A(1'b0), .B(n1bit_with_restore_21_divisior_prop), .Cin(1'b1), .Cout(n1bit_with_restore_22_cout),
    .Decider(n1bit_with_restore_23_decision), .Divisior_Prop(n1bit_with_restore_22_divisior_prop),
    .Output(n1bit_with_restore_22_output));  // open: Decision
  _1Bit___With_Restore u_1bit_with_restore_23 (
    .A(n1bit_with_restore_21_output), .B(n1bit_with_restore_16_divisior_prop),
    .Cin(n1bit_with_restore_22_cout), .Decision(n1bit_with_restore_23_decision),
    .Cout(n1bit_with_restore_23_cout), .Decider(n1bit_with_restore_17_decision),
    .Divisior_Prop(n1bit_with_restore_23_divisior_prop), .Output(n1bit_with_restore_23_output));
  _1Bit___With_Restore u_1bit_with_restore_24 (
    .A(n1bit_with_restore_23_output), .B(n1bit_with_restore_17_divisior_prop),
    .Cin(n1bit_with_restore_25_cout), .Decision(n1bit_with_restore_24_decision),
    .Cout(n1bit_with_restore_24_cout), .Decider(n1bit_with_restore_18_decision),
    .Divisior_Prop(n1bit_with_restore_24_divisior_prop), .Output(n1bit_with_restore_24_output));
  _1Bit___With_Restore u_1bit_with_restore_25 (
    .A(n1bit_with_restore_22_output), .B(n1bit_with_restore_23_divisior_prop),
    .Cin(n1bit_with_restore_32_cout), .Decision(n1bit_with_restore_25_decision),
    .Cout(n1bit_with_restore_25_cout), .Decider(n1bit_with_restore_24_decision),
    .Divisior_Prop(n1bit_with_restore_25_divisior_prop), .Output(n1bit_with_restore_25_output));
  _1Bit___With_Restore u_1bit_with_restore_26 (
    .A(n1bit_with_restore_25_output), .B(n1bit_with_restore_24_divisior_prop),
    .Cin(n1bit_with_restore_33_cout), .Decision(n1bit_with_restore_26_decision),
    .Cout(n1bit_with_restore_26_cout), .Decider(n1bit_with_restore_27_decision),
    .Divisior_Prop(n1bit_with_restore_26_divisior_prop), .Output(n1bit_with_restore_26_output));
  _1Bit___With_Restore u_1bit_with_restore_27 (
    .A(n1bit_with_restore_24_output), .B(n1bit_with_restore_18_divisior_prop),
    .Cin(n1bit_with_restore_26_cout), .Decision(n1bit_with_restore_27_decision),
    .Cout(n1bit_with_restore_27_cout), .Decider(n1bit_with_restore_19_decision),
    .Divisior_Prop(n1bit_with_restore_27_divisior_prop), .Output(n1bit_with_restore_27_output));
  _1Bit___With_Restore u_1bit_with_restore_28 (
    .A(n1bit_with_restore_26_output), .B(n1bit_with_restore_27_divisior_prop),
    .Cin(n1bit_with_restore_34_cout), .Decision(n1bit_with_restore_28_decision),
    .Cout(n1bit_with_restore_28_cout), .Decider(n1bit_with_restore_29_decision),
    .Divisior_Prop(n1bit_with_restore_28_divisior_prop), .Output(n1bit_with_restore_28_output));
  _1Bit___With_Restore u_1bit_with_restore_29 (
    .A(n1bit_with_restore_27_output), .B(n1bit_with_restore_19_divisior_prop),
    .Cin(n1bit_with_restore_28_cout), .Decision(n1bit_with_restore_29_decision),
    .Cout(n1bit_with_restore_29_cout), .Decider(n1bit_with_restore_20_decision),
    .Divisior_Prop(n1bit_with_restore_29_divisior_prop), .Output(n1bit_with_restore_29_output));
  _1Bit___With_Restore u_1bit_with_restore_30 (
    .A(n1bit_with_restore_28_output), .B(n1bit_with_restore_29_divisior_prop),
    .Cin(n1bit_with_restore_35_cout), .Decision(n1bit_with_restore_30_decision),
    .Cout(n1bit_with_restore_30_cout), .Decider(n1bit_with_restore_31_decision));  // open: Divisior_Prop, Output
  _1Bit___With_Restore u_1bit_with_restore_31 (
    .A(n1bit_with_restore_29_output), .B(n1bit_with_restore_20_divisior_prop),
    .Cin(n1bit_with_restore_30_cout), .Decision(n1bit_with_restore_31_decision), .Cout(q6), .Decider(q6));  // open: Divisior_Prop, Output
  _1Bit___With_Restore u_1bit_with_restore_32 (
    .A(1'b0), .B(n1bit_with_restore_22_divisior_prop), .Cin(1'b1), .Cout(n1bit_with_restore_32_cout),
    .Decider(n1bit_with_restore_25_decision), .Divisior_Prop(n1bit_with_restore_32_divisior_prop),
    .Output(n1bit_with_restore_32_output));  // open: Decision
  _1Bit___With_Restore u_1bit_with_restore_33 (
    .A(n1bit_with_restore_32_output), .B(n1bit_with_restore_25_divisior_prop),
    .Cin(n1bit_with_restore_36_cout), .Decision(n1bit_with_restore_33_decision),
    .Cout(n1bit_with_restore_33_cout), .Decider(n1bit_with_restore_26_decision),
    .Divisior_Prop(n1bit_with_restore_33_divisior_prop), .Output(n1bit_with_restore_33_output));
  _1Bit___With_Restore u_1bit_with_restore_34 (
    .A(n1bit_with_restore_33_output), .B(n1bit_with_restore_26_divisior_prop),
    .Cin(n1bit_with_restore_37_cout), .Decision(n1bit_with_restore_34_decision),
    .Cout(n1bit_with_restore_34_cout), .Decider(n1bit_with_restore_28_decision),
    .Divisior_Prop(n1bit_with_restore_34_divisior_prop), .Output(n1bit_with_restore_34_output));
  _1Bit___With_Restore u_1bit_with_restore_35 (
    .A(n1bit_with_restore_34_output), .B(n1bit_with_restore_28_divisior_prop),
    .Cin(n1bit_with_restore_38_cout), .Decision(n1bit_with_restore_35_decision),
    .Cout(n1bit_with_restore_35_cout), .Decider(n1bit_with_restore_30_decision));  // open: Divisior_Prop, Output
  _1Bit___With_Restore u_1bit_with_restore_36 (
    .A(1'b0), .B(n1bit_with_restore_32_divisior_prop), .Cin(1'b1), .Cout(n1bit_with_restore_36_cout),
    .Decider(n1bit_with_restore_33_decision), .Divisior_Prop(n1bit_with_restore_36_divisior_prop),
    .Output(n1bit_with_restore_36_output));  // open: Decision
  _1Bit___With_Restore u_1bit_with_restore_37 (
    .A(n1bit_with_restore_36_output), .B(n1bit_with_restore_33_divisior_prop),
    .Cin(n1bit_with_restore_39_cout), .Decision(n1bit_with_restore_37_decision),
    .Cout(n1bit_with_restore_37_cout), .Decider(n1bit_with_restore_34_decision),
    .Divisior_Prop(n1bit_with_restore_37_divisior_prop), .Output(n1bit_with_restore_37_output));
  _1Bit___With_Restore u_1bit_with_restore_38 (
    .A(n1bit_with_restore_37_output), .B(n1bit_with_restore_34_divisior_prop),
    .Cin(n1bit_with_restore_41_cout), .Decision(n1bit_with_restore_38_decision),
    .Cout(n1bit_with_restore_38_cout), .Decider(n1bit_with_restore_35_decision));  // open: Divisior_Prop, Output
  _1Bit___With_Restore u_1bit_with_restore_39 (
    .A(1'b0), .B(n1bit_with_restore_36_divisior_prop), .Cin(1'b1), .Cout(n1bit_with_restore_39_cout),
    .Decider(n1bit_with_restore_37_decision), .Divisior_Prop(n1bit_with_restore_39_divisior_prop),
    .Output(n1bit_with_restore_39_output));  // open: Decision
  _1Bit___With_Restore u_1bit_with_restore_40 (
    .A(1'b0), .B(n1bit_with_restore_39_divisior_prop), .Cin(1'b1), .Cout(n1bit_with_restore_40_cout),
    .Decider(n1bit_with_restore_41_decision));  // open: Decision, Divisior_Prop, Output
  _1Bit___With_Restore u_1bit_with_restore_41 (
    .A(n1bit_with_restore_39_output), .B(n1bit_with_restore_37_divisior_prop),
    .Cin(n1bit_with_restore_40_cout), .Decision(n1bit_with_restore_41_decision),
    .Cout(n1bit_with_restore_41_cout), .Decider(n1bit_with_restore_38_decision));  // open: Divisior_Prop, Output

  // Notes on the sheet:
  //   .
  //   .
endmodule

module Profit___1 (
  input  d1,
  input  d0,
  output q1,
  output q0
);

  wire adder_1_cout, not_1_out, not_2_out;

  not not_1 (not_1_out, 1'b1);
  not not_2 (not_2_out, 1'b0);
  Adder #(.width(1)) adder_1 (.a(d1), .b(not_1_out), .out(q1), .cin(1'b1), .cout(adder_1_cout));
  Adder #(.width(1)) adder_2 (.a(d0), .b(not_2_out), .out(q0), .cin(adder_1_cout));  // open: cout
endmodule

module Profit_Decoder (
  input  dMSB,
  input  d0,
  input  d1,
  input  d2,
  input  d3,
  input  d4,
  output D10,
  output D0_2,
  output D6,
  output D20,
  output D1_2,
  output D7,
  output D8,
  output D2_2,
  output D9,
  output D11,
  output D12,
  output D3_2,
  output D4_2,
  output D5,
  output D13,
  output D14,
  output D15,
  output D17,
  output D16,
  output D18,
  output D19
);

  wire and_2_out, and_3_out, and_4_out, and_5_out, and_7_out, and_8_out, and_17_out, and_18_out, not_1_out,
       not_2_out, not_3_out, not_4_out, not_5_out, not_6_out, xor_1_out, xor_2_out;

  and and_1 (D20, dMSB, not_2_out, not_3_out, not_4_out, not_5_out, not_6_out);
  and and_2 (and_2_out, not_1_out, d0, not_3_out, not_4_out, d3, d4);
  and and_3 (and_3_out, not_1_out, d0, not_3_out, d2, not_5_out, not_6_out);
  and and_4 (and_4_out, not_1_out, d0, d1, not_4_out, d3, d4);
  and and_5 (and_5_out, not_1_out, d0, d1, d2, not_5_out, not_6_out);
  or or_1 (D12, and_2_out, and_3_out);
  or or_2 (D17, and_4_out, and_5_out);
  xor xor_1 (xor_1_out, d4, d3);
  and and_6 (D10, not_1_out, d0, not_3_out, not_4_out, not_5_out, not_6_out);
  and and_7 (and_7_out, not_1_out, not_2_out, d1, not_4_out, d3, d4);
  and and_8 (and_8_out, not_1_out, not_2_out, d2, not_5_out, not_6_out, d1);
  and and_9 (D11, not_1_out, d0, not_3_out, not_4_out, xor_1_out);
  and and_10 (D13, not_1_out, d0, not_3_out, d2, not_5_out, d4);
  and and_11 (D14, not_1_out, d0, not_3_out, d2, d3);
  not not_1 (not_1_out, dMSB);
  not not_2 (not_2_out, d0);
  or or_3 (D7, and_7_out, and_8_out);
  not not_3 (not_3_out, d1);
  not not_4 (not_4_out, d2);
  not not_5 (not_5_out, d3);
  not not_6 (not_6_out, d4);
  and and_12 (D19, not_1_out, d0, d1, d2, d3);
  and and_13 (D15, not_1_out, d0, d1, not_4_out, not_5_out, not_6_out);
  and and_14 (D16, not_1_out, d0, d1, not_4_out, xor_1_out);
  and and_15 (D0_2, not_1_out, not_2_out, not_3_out, not_4_out, not_5_out, not_6_out);
  xor xor_2 (xor_2_out, d3, d4);
  and and_16 (D1_2, not_1_out, not_2_out, not_3_out, not_4_out, xor_2_out);
  and and_17 (and_17_out, d3, d4, not_1_out, not_2_out, not_3_out, not_4_out);
  or or_4 (D2_2, and_17_out, and_18_out);
  and and_18 (and_18_out, not_1_out, not_2_out, not_3_out, not_5_out, not_6_out, d2);
  and and_19 (D3_2, d2, not_5_out, not_2_out, not_1_out, not_3_out, d4);
  and and_20 (D4_2, d2, d3, not_2_out, not_3_out, not_1_out);
  and and_21 (D5, d1, not_6_out, not_5_out, not_4_out, not_2_out, not_1_out);
  and and_22 (D6, not_4_out, not_1_out, not_2_out, xor_2_out, d1);
  and and_23 (D8, not_1_out, not_2_out, d1, d2, xor_2_out, d4);
  and and_24 (D18, not_1_out, d0, d1, d2, not_5_out, d4);
  and and_25 (D9, not_1_out, not_2_out, d1, d2, d3);
endmodule

module Profit__Decoder (
  input  dMSB,
  input  d0,
  input  d1,
  input  d2,
  input  d3,
  input  d4,
  output D0_2,
  output D11,
  output D1_2,
  output D12,
  output D2_2,
  output D13,
  output D3_2,
  output D14,
  output D4_2,
  output D15,
  output D5,
  output D16,
  output D6,
  output D17,
  output D7,
  output D18,
  output D8,
  output D19,
  output D9,
  output D20,
  output D10
);

  wire and_11_out, and_12_out, and_13_out, and_14_out, not_1_out, not_2_out, not_3_out, not_4_out, not_5_out,
       not_6_out, not_7_out, not_8_out, not_9_out, not_10_out, not_11_out, not_12_out, not_13_out,
       not_14_out, not_15_out, not_16_out, not_17_out, not_18_out, not_19_out, not_20_out, not_21_out,
       not_22_out, not_23_out, not_24_out, not_25_out, not_26_out, not_27_out, not_28_out, not_29_out,
       not_30_out, not_31_out, not_32_out, not_33_out, not_34_out, not_35_out, not_36_out, not_37_out,
       not_38_out, not_39_out, not_40_out, not_41_out, not_42_out, not_43_out, not_44_out, not_45_out,
       not_46_out, not_47_out, not_48_out, not_49_out, not_50_out, not_51_out, not_52_out, not_53_out,
       not_54_out, not_55_out, not_56_out, not_57_out, not_58_out, not_59_out, not_60_out, not_61_out,
       not_62_out, not_63_out, not_64_out, not_65_out, not_66_out, not_67_out, not_68_out, not_69_out,
       not_70_out, not_71_out, or_1_out, or_2_out, xor_1_out, xor_2_out;

  not not_1 (not_1_out, dMSB);
  and and_1 (D11, not_1_out, d0, not_2_out, not_3_out, xor_1_out);
  not not_2 (not_2_out, d1);
  not not_3 (not_3_out, d2);
  not not_4 (not_4_out, dMSB);
  and and_2 (D12, not_4_out, d0, not_5_out, or_1_out);
  not not_5 (not_5_out, d1);
  not not_6 (not_6_out, dMSB);
  not not_7 (not_7_out, d1);
  and and_3 (D13, not_6_out, d0, not_7_out, d2, not_8_out, d4);
  not not_8 (not_8_out, d3);
  not not_9 (not_9_out, dMSB);
  not not_10 (not_10_out, d1);
  and and_4 (D14, not_9_out, d0, not_10_out, d2, d3);
  not not_11 (not_11_out, dMSB);
  and and_5 (D15, not_11_out, d0, d1, not_12_out, not_13_out, not_14_out);
  not not_12 (not_12_out, d2);
  not not_13 (not_13_out, d3);
  not not_14 (not_14_out, d4);
  not not_15 (not_15_out, dMSB);
  and and_6 (D16, not_15_out, d0, d1, not_16_out, xor_1_out);
  not not_16 (not_16_out, d2);
  not not_17 (not_17_out, dMSB);
  and and_7 (D17, not_17_out, d0, d1, or_1_out);
  not not_18 (not_18_out, dMSB);
  and and_8 (D18, not_18_out, d0, d1, d2, not_19_out, d4);
  not not_19 (not_19_out, d3);
  not not_20 (not_20_out, dMSB);
  and and_9 (D19, not_20_out, d0, d1, d2, d3);
  not not_21 (not_21_out, d0);
  not not_22 (not_22_out, d1);
  and and_10 (D20, dMSB, not_21_out, not_22_out, not_23_out, not_24_out, not_25_out);
  not not_23 (not_23_out, d2);
  not not_24 (not_24_out, d3);
  not not_25 (not_25_out, d4);
  or or_1 (or_1_out, and_11_out, and_12_out);
  and and_11 (and_11_out, not_26_out, d3, d4);
  and and_12 (and_12_out, d2, not_27_out, not_28_out);
  xor xor_1 (xor_1_out, d3, d4);
  not not_26 (not_26_out, d2);
  not not_27 (not_27_out, d3);
  not not_28 (not_28_out, d4);
  not not_29 (not_29_out, d2);
  and and_13 (and_13_out, not_29_out, d3, d4);
  and and_14 (and_14_out, d2, not_30_out, not_31_out);
  not not_30 (not_30_out, d3);
  not not_31 (not_31_out, d4);
  or or_2 (or_2_out, and_13_out, and_14_out);
  xor xor_2 (xor_2_out, d3, d4);
  not not_32 (not_32_out, dMSB);
  not not_33 (not_33_out, d0);
  not not_34 (not_34_out, d1);
  not not_35 (not_35_out, d2);
  not not_36 (not_36_out, d3);
  not not_37 (not_37_out, d4);
  not not_38 (not_38_out, dMSB);
  not not_39 (not_39_out, d0);
  not not_40 (not_40_out, d1);
  not not_41 (not_41_out, d2);
  not not_42 (not_42_out, dMSB);
  not not_43 (not_43_out, d0);
  not not_44 (not_44_out, d1);
  not not_45 (not_45_out, dMSB);
  not not_46 (not_46_out, d0);
  not not_47 (not_47_out, d1);
  not not_48 (not_48_out, d3);
  not not_49 (not_49_out, dMSB);
  not not_50 (not_50_out, d0);
  not not_51 (not_51_out, d1);
  not not_52 (not_52_out, dMSB);
  not not_53 (not_53_out, d0);
  not not_54 (not_54_out, d2);
  not not_55 (not_55_out, d3);
  not not_56 (not_56_out, d4);
  not not_57 (not_57_out, dMSB);
  not not_58 (not_58_out, d0);
  not not_59 (not_59_out, d2);
  not not_60 (not_60_out, dMSB);
  not not_61 (not_61_out, d0);
  not not_62 (not_62_out, dMSB);
  not not_63 (not_63_out, d0);
  not not_64 (not_64_out, d3);
  not not_65 (not_65_out, dMSB);
  not not_66 (not_66_out, d0);
  not not_67 (not_67_out, dMSB);
  not not_68 (not_68_out, d1);
  not not_69 (not_69_out, d2);
  not not_70 (not_70_out, d3);
  not not_71 (not_71_out, d4);
  and and_15 (D0_2, not_32_out, not_33_out, not_34_out, not_35_out, not_36_out, not_37_out);
  and and_16 (D1_2, not_38_out, not_39_out, not_40_out, not_41_out, xor_2_out);
  and and_17 (D2_2, not_42_out, not_43_out, not_44_out, or_2_out);
  and and_18 (D3_2, not_45_out, not_46_out, not_47_out, d2, not_48_out, d4);
  and and_19 (D4_2, not_49_out, not_50_out, not_51_out, d2, d3);
  and and_20 (D5, not_52_out, not_53_out, d1, not_54_out, not_55_out, not_56_out);
  and and_21 (D6, not_57_out, not_58_out, d1, not_59_out, xor_2_out);
  and and_22 (D7, not_60_out, not_61_out, d1, or_2_out);
  and and_23 (D8, not_62_out, not_63_out, d1, d2, not_64_out, d4);
  and and_24 (D9, not_65_out, not_66_out, d1, d2, d3);
  and and_25 (D10, not_67_out, d0, not_68_out, not_69_out, not_70_out, not_71_out);
endmodule
